# Fritzing sketch uso de biblioteca (saved by Fritzing 0.9.3b)

parts:
  Componente1 = Arduino Uno (Rev3)
  J1 = Basic Servo

nets:
  N1: Componente1.D9_PWM, J1.pulse
  5V: Componente1.5V, J1.vcc
  GND: Componente1.GND, J1.gnd
